// Digital circuit BCD_to_Decimal.dig as structural Verilog
module BCD_to_Decimal (
  input  b2,
  input  b1,
  input  b0,
  input  b3,
  output D_0,
  output D_1,
  output D_2,
  output D_3,
  output D_4,
  output D_5,
  output D_6,
  output D_7,
  output D_8,
  output D_9,
  output D_10,
  output D_11,
  output D_12,
  output D_13,
  output D_14,
  output D_15
);

  wire not_1_out, not_2_out, not_3_out, not_4_out;

  not not_1 (not_1_out, b3);
  not not_2 (not_2_out, b2);
  not not_3 (not_3_out, b1);
  not not_4 (not_4_out, b0);
  and and_1 (D_0, not_2_out, not_3_out, not_4_out, not_1_out);
  and and_2 (D_1, not_2_out, not_3_out, b0, not_1_out);
  and and_3 (D_2, not_2_out, b1, not_4_out, not_1_out);
  and and_4 (D_3, not_2_out, b1, b0, not_1_out);
  and and_5 (D_4, b2, not_3_out, not_4_out, not_1_out);
  and and_6 (D_5, b2, not_3_out, b0, not_1_out);
  and and_7 (D_6, b2, b1, not_4_out, not_1_out);
  and and_8 (D_7, b2, b1, b0, not_1_out);
  and and_9 (D_8, not_2_out, not_3_out, not_4_out, b3);
  and and_10 (D_9, not_2_out, not_3_out, b0, b3);
  and and_11 (D_10, not_2_out, b1, not_4_out, b3);
  and and_12 (D_11, not_2_out, b1, b0, b3);
  and and_13 (D_12, b2, not_3_out, not_4_out, b3);
  and and_14 (D_13, b2, not_3_out, b0, b3);
  and and_15 (D_14, b2, b1, not_4_out, b3);
  and and_16 (D_15, b2, b1, b0, b3);
endmodule
