// Digital circuit BCD_to_sevensegment.dig as structural Verilog
module BCD_to_sevensegment (
);

  wire and_1_out, and_2_out, and_3_out, and_4_out, and_5_out, and_6_out, and_7_out, and_8_out, and_9_out,
       and_10_out, and_11_out, and_12_out, and_13_out, and_14_out, and_15_out, and_16_out, and_17_out,
       and_18_out, and_19_out, and_20_out, and_21_out, and_22_out, and_23_out, and_24_out, and_25_out,
       and_26_out, and_27_out, and_28_out, and_29_out, and_30_out, and_31_out, and_32_out, and_33_out,
       and_34_out, and_35_out, and_36_out, and_37_out, and_38_out, and_39_out, and_40_out, and_41_out,
       not_1_out, not_2_out, not_3_out, not_4_out, not_5_out, or_1_out, or_2_out, or_3_out, or_4_out,
       or_5_out, or_6_out, or_7_out, undriven, undriven_2, undriven_3, undriven_4, undriven_5;

  not not_1 (not_1_out, undriven_5);
  not not_2 (not_2_out, undriven_4);
  not not_3 (not_3_out, undriven_3);
  not not_4 (not_4_out, undriven_2);
  not not_5 (not_5_out, undriven);
  and and_1 (and_1_out, not_1_out, not_5_out, undriven_4);
  and and_2 (and_2_out, not_1_out, undriven_2, undriven_3);
  and and_3 (and_3_out, not_5_out, not_4_out, not_3_out);
  and and_4 (and_4_out, undriven, undriven_3, not_2_out);
  and and_5 (and_5_out, not_4_out, not_3_out, undriven_4);
  and and_6 (and_6_out, undriven_2, not_2_out);
  and and_7 (and_7_out, not_1_out, undriven, not_4_out, undriven_4);
  and and_8 (and_8_out, not_1_out, not_5_out, not_3_out);
  and and_9 (and_9_out, not_5_out, not_4_out, not_2_out);
  and and_10 (and_10_out, undriven, undriven_2, not_2_out);
  and and_11 (and_11_out, not_4_out, not_3_out);
  and and_12 (and_12_out, not_3_out, not_2_out);
  and and_13 (and_13_out, not_1_out, undriven, not_4_out);
  and and_14 (and_14_out, not_1_out, not_3_out, undriven_4);
  and and_15 (and_15_out, undriven, not_2_out);
  and and_16 (and_16_out, not_4_out, not_3_out);
  and and_17 (and_17_out, undriven_3, not_2_out);
  and and_18 (and_18_out, not_1_out, undriven, undriven_2, not_3_out);
  and and_19 (and_19_out, not_1_out, not_5_out, undriven_3, undriven_4);
  and and_20 (and_20_out, not_1_out, not_4_out, undriven_4);
  and and_21 (and_21_out, undriven, not_4_out, undriven_3, not_2_out);
  and and_22 (and_22_out, not_5_out, not_4_out, not_3_out);
  and and_23 (and_23_out, not_5_out, undriven_2, not_2_out);
  and and_24 (and_24_out, undriven_2, not_3_out, not_2_out);
  and and_25 (and_25_out, not_4_out, not_3_out, undriven_4);
  and and_26 (and_26_out, not_1_out, undriven_2, undriven_4);
  and and_27 (and_27_out, not_1_out, undriven_3, undriven_4);
  and and_28 (and_28_out, not_5_out, not_4_out, not_3_out);
  and and_29 (and_29_out, not_5_out, undriven_2, not_2_out);
  and and_30 (and_30_out, not_1_out, not_5_out, not_4_out);
  and and_31 (and_31_out, not_1_out, undriven_2, undriven_4);
  and and_32 (and_32_out, not_5_out, not_4_out, not_3_out);
  and and_33 (and_33_out, not_5_out, undriven_3, not_2_out);
  and and_34 (and_34_out, not_4_out, undriven_3, not_2_out);
  and and_35 (and_35_out, not_4_out, not_3_out, undriven_4);
  and and_36 (and_36_out, not_1_out, undriven, undriven_4);
  and and_37 (and_37_out, not_1_out, undriven_2, undriven_4);
  and and_38 (and_38_out, not_5_out, undriven_2, not_2_out);
  and and_39 (and_39_out, undriven_2, not_3_out, not_2_out);
  and and_40 (and_40_out, not_4_out, undriven_3, not_2_out);
  and and_41 (and_41_out, not_4_out, not_3_out, undriven_4);
  or or_1 (or_1_out, and_1_out, and_2_out, and_3_out, and_4_out, and_5_out, and_6_out);
  or or_2 (or_2_out, and_7_out, and_8_out, and_9_out, and_10_out, and_11_out, and_12_out);
  or or_3 (or_3_out, and_13_out, and_14_out, and_15_out, and_16_out, and_17_out);
  or or_4 (or_4_out, and_18_out, and_19_out, and_20_out, and_21_out, and_22_out, and_23_out, and_24_out, and_25_out);
  or or_5 (or_5_out, and_26_out, and_27_out, and_28_out, and_29_out);
  or or_6 (or_6_out, and_30_out, and_31_out, and_32_out, and_33_out, and_34_out, and_35_out);
  or or_7 (or_7_out, and_36_out, and_37_out, and_38_out, and_39_out, and_40_out, and_41_out);
  Seven_Seg seven_seg_1 (
    .a(or_1_out), .b(or_2_out), .c(or_3_out), .d(or_4_out), .e(or_5_out), .f(or_6_out), .g(or_7_out),
    .dp(1'b0));

  // Notes on the sheet:
  //   1
  //   2
  //   3
  //   5
  //   6
  //   7
  //   4
endmodule
