// Digital circuit Ch6-01 4-bit register with parallel load.dig as structural Verilog
module Ch6_01_4_bit_register_with_parallel_load (
  input  I_0,
  input  CLK,
  input  Clear,
  input  I_1,
  input  I_2,
  input  I_3,
  output A_0,
  output A_1,
  output A_2,
  output A_3
);

  D_FF_AS d_ff_as_1 (.Set(1'b0), .D(I_0), .C(CLK), .Clr(Clear), .Q(A_0));  // open: nQ
  D_FF_AS d_ff_as_2 (.Set(1'b0), .D(I_1), .C(CLK), .Clr(Clear), .Q(A_1));  // open: nQ
  D_FF_AS d_ff_as_3 (.Set(1'b0), .D(I_2), .C(CLK), .Clr(Clear), .Q(A_2));  // open: nQ
  D_FF_AS d_ff_as_4 (.Set(1'b0), .D(I_3), .C(CLK), .Clr(Clear), .Q(A_3));  // open: nQ
endmodule
