// Digital circuit Full Adder 4-bit.dig as structural Verilog
module Full_Adder_4_bit (
  input  B_0,
  input  A_0,
  input  C_in,
  input  B_1,
  input  A_1,
  input  B_2,
  input  A_2,
  input  B_3,
  input  A_3,
  output S_0,
  output S_1,
  output S_2,
  output S_3,
  output C_out
);

  wire FA_0_c_out, FA_1_c_out, FA_2_c_out;

  Full_Adder FA_3 (.A(A_3), .B(B_3), .C_in(FA_2_c_out), .S(S_3), .C_out(C_out));
  Full_Adder FA_2 (.A(A_2), .B(B_2), .C_in(FA_1_c_out), .S(S_2), .C_out(FA_2_c_out));
  Full_Adder FA_1 (.A(A_1), .B(B_1), .C_in(FA_0_c_out), .S(S_1), .C_out(FA_1_c_out));
  Full_Adder FA_0 (.A(A_0), .B(B_0), .C_in(C_in), .S(S_0), .C_out(FA_0_c_out));
endmodule
