// Digital circuit Reset.dig as structural Verilog
module Reset (
  input  plus,
  input  in_2,
  input  in_3,
  input  in_4,
  input  C,
  output Reset
);

  or or_1 (Reset, plus, in_2, in_3, in_4, C);
endmodule
