// Digital circuit Term_Project.dig as structural Verilog
module Term_Project (
  input  [3:0] in_1,
  input  [3:0] in_2,
  input  [7:0] in_3,
  input  [3:0] in_4,
  input  [7:0] in_5,
  input  [3:0] in_6,
  input  [7:0] in_7,
  input  [7:0] in_8,
  input  [3:0] in_9,
  input  [3:0] in_10,
  input  [7:0] in_11,
  input  [3:0] in_12,
  input  [7:0] in_13,
  input  [3:0] in_14,
  input  [7:0] in_15,
  input  [7:0] in_16,
  input  [15:0] in_17,
  input  [15:0] in_18,
  input  [15:0] in_19,
  input  [15:0] in_20,
  output [15:0] out_21,
  output [15:0] out_22,
  output [15:0] out_23,
  output [15:0] out_24,
  output [15:0] out_25,
  output [15:0] out_26
);

  wire _0, _1, _2, _3, _4, _5, _6, _7, _8, _9, A0, A1, A2, A3, alt, alt1, alt2, alt3, alt4, alt5, alt6, alt7,
       b0, B1, b1_t, B2, b2_t, B3, b3_t, B4, C, clk, clk1, d_ff_1_q, d_ff_2_q, d_ff_3_q, d_ff_4_q, eksi, eq,
       error, I0, I1, I2, I3, M0, M1, M2, M3, M4, M5, M6, M7, M8, M9, M10, M11, M12, M13, M14, M15, orta,
       orta1, orta2, orta3, orta4, orta5, orta6, orta7, plus, \sağ_alt , \sağ_alt1 , \sağ_alt2 , \sağ_alt3 ,
       \sağ_alt4 , \sağ_alt5 , \sağ_alt6 , \sağ_alt7 , \sağ_üst , \sağ_üst1 , \sağ_üst2 , \sağ_üst3 ,
       \sağ_üst4 , \sağ_üst5 , \sağ_üst6 , \sağ_üst7 , sol_alt, sol_alt1, sol_alt2, sol_alt3, sol_alt4,
       sol_alt5, sol_alt6, sol_alt7, \sol_üst , \sol_üst1 , \sol_üst2 , \sol_üst3 , \sol_üst4 , \sol_üst5 ,
       \sol_üst6 , \sol_üst7 , tunnel, tunnel_t, tunnel_t_t, Y0, Y1, Y2, Y3, \üst , \üst1 , \üst2 , \üst3 ,
       \üst4 , \üst5 , \üst6 , \üst7 ;
  wire [7:0] mul_1_mul, mul_2_mul, mul_3_mul, mul_4_mul, mul_5_mul, mul_6_mul, mul_7_mul, mul_8_mul;
  wire [15:0] add_1_s, add_2_s, add_3_s, add_4_s, add_5_s, add_6_s, add_7_s, add_8_s, add_9_s, add_10_s,
       add_11_s, add_12_s, add_13_s, add_14_s, add_15_s, add_16_s, add_17_s, add_18_s, add_21_s, add_22_s,
       add_23_s, add_24_s, get1, get2, mul_9_mul, mul_10_mul, mul_11_mul, mul_12_mul, mul_13_mul, mul_14_mul,
       mul_15_mul, mul_16_mul, \onlar_basamağı_q , \operation_1_çıktı , \yüzler_basamağı_q ;

  clk clk_1 (._1(_1), ._2(_4), ._3(_3), ._4(_2), ._5(_5), ._6(_6), ._7(_7), ._8(_9), ._9(_8), ._0(_0), .clk(clk));
  decimal_to_bcd decimal_to_bcd_1 (
    ._1(_1), ._3(_3), ._2(_2), ._5(_5), ._4(_4), ._6(_6), ._7(_7), ._9(_9), ._8(_8), ._0(_0), .B0(b0),
    .B1(b1_t), .B2(b2_t), .B3(b3_t));
  opclk operator_clock (.plus(plus), .in_2(tunnel_t), .in_3(tunnel), .in_4(tunnel_t_t), .C(C), .clk1(clk1));
  Ch6_01_4_bit_register_with_parallel_load ch6_01_4_bit_register_with_parallel_load_1 (
    .I_0(b0), .CLK(clk), .Clear(clk1), .I_1(b1_t), .I_2(b2_t), .I_3(b3_t), .A_0(I0), .A_1(I1), .A_2(I2),
    .A_3(I3));
  Ch6_01_4_bit_register_with_parallel_load ch6_01_4_bit_register_with_parallel_load_2 (
    .I_0(I0), .CLK(clk1), .Clear(C), .I_1(I1), .I_2(I2), .I_3(I3), .A_0(M0), .A_1(M1), .A_2(M2), .A_3(M3));
  Ch6_01_4_bit_register_with_parallel_load ch6_01_4_bit_register_with_parallel_load_3 (
    .I_0(I0), .CLK(clk), .Clear(clk1), .I_1(I1), .I_2(I2), .I_3(I3), .A_0(A0), .A_1(A1), .A_2(A2), .A_3(A3));
  Ch6_01_4_bit_register_with_parallel_load ch6_01_4_bit_register_with_parallel_load_4 (
    .I_0(A0), .CLK(clk1), .Clear(C), .I_1(A1), .I_2(A2), .I_3(A3), .A_0(M4), .A_1(M5), .A_2(M6), .A_3(M7));
  Ch6_01_4_bit_register_with_parallel_load ch6_01_4_bit_register_with_parallel_load_5 (
    .I_0(A0), .CLK(clk), .Clear(clk1), .I_1(A1), .I_2(A2), .I_3(A3), .A_0(B1), .A_1(B2), .A_2(B3), .A_3(B4));
  Ch6_01_4_bit_register_with_parallel_load ch6_01_4_bit_register_with_parallel_load_6 (
    .I_0(B1), .CLK(clk1), .Clear(C), .I_1(B2), .I_2(B3), .I_3(B4), .A_0(M8), .A_1(M9), .A_2(M10), .A_3(M11));
  Ch6_01_4_bit_register_with_parallel_load ch6_01_4_bit_register_with_parallel_load_7 (
    .I_0(B1), .CLK(clk), .Clear(clk1), .I_1(B2), .I_2(B3), .I_3(B4), .A_0(Y0), .A_1(Y1), .A_2(Y2), .A_3(Y3));
  Ch6_01_4_bit_register_with_parallel_load ch6_01_4_bit_register_with_parallel_load_8 (
    .I_0(Y0), .CLK(clk1), .Clear(C), .I_1(Y1), .I_2(Y2), .I_3(Y3), .A_0(M12), .A_1(M13), .A_2(M14), .A_3(M15));
  emb emb_1 (
    .b3(Y3), .b2(Y2), .b1(Y1), .b0(Y0), .\sağ_alt (\sağ_alt ), .orta(orta), .\sağ_üst (\sağ_üst ),
    .\sol_üst (\sol_üst ), .\üst (\üst ), .sol_alt(sol_alt), .alt(alt));
  emb emb_2 (
    .b3(M15), .b2(M14), .b1(M13), .b0(M12), .\sağ_alt (\sağ_alt4 ), .orta(orta4), .\sağ_üst (\sağ_üst4 ),
    .\sol_üst (\sol_üst4 ), .\üst (\üst4 ), .sol_alt(sol_alt4), .alt(alt4));
  emb emb_3 (
    .b3(B4), .b2(B3), .b1(B2), .b0(B1), .\sağ_alt (\sağ_alt1 ), .orta(orta1), .\sağ_üst (\sağ_üst1 ),
    .\sol_üst (\sol_üst1 ), .\üst (\üst1 ), .sol_alt(sol_alt1), .alt(alt1));
  emb emb_4 (
    .b3(M11), .b2(M10), .b1(M9), .b0(M8), .\sağ_alt (\sağ_alt5 ), .orta(orta5), .\sağ_üst (\sağ_üst5 ),
    .\sol_üst (\sol_üst5 ), .\üst (\üst5 ), .sol_alt(sol_alt5), .alt(alt5));
  emb emb_5 (
    .b3(A3), .b2(A2), .b1(A1), .b0(A0), .\sağ_alt (\sağ_alt2 ), .orta(orta2), .\sağ_üst (\sağ_üst2 ),
    .\sol_üst (\sol_üst2 ), .\üst (\üst2 ), .sol_alt(sol_alt2), .alt(alt2));
  emb emb_6 (
    .b3(M7), .b2(M6), .b1(M5), .b0(M4), .\sağ_alt (\sağ_alt6 ), .orta(orta6), .\sağ_üst (\sağ_üst6 ),
    .\sol_üst (\sol_üst6 ), .\üst (\üst6 ), .sol_alt(sol_alt6), .alt(alt6));
  emb emb_7 (
    .b3(I3), .b2(I2), .b1(I1), .b0(I0), .\sağ_alt (\sağ_alt3 ), .orta(orta3), .\sağ_üst (\sağ_üst3 ),
    .\sol_üst (\sol_üst3 ), .\üst (\üst3 ), .sol_alt(sol_alt3), .alt(alt3));
  emb emb_8 (
    .b3(M3), .b2(M2), .b1(M1), .b0(M0), .\sağ_alt (\sağ_alt7 ), .orta(orta7), .\sağ_üst (\sağ_üst7 ),
    .\sol_üst (\sol_üst7 ), .\üst (\üst7 ), .sol_alt(sol_alt7), .alt(alt7));
  Seven_Seg seven_seg_1 (
    .a(\üst4 ), .b(\sağ_üst4 ), .c(\sağ_alt4 ), .d(alt4), .e(sol_alt4), .f(\sol_üst4 ), .g(orta4), .dp(1'b1));
  Seven_Seg seven_seg_2 (
    .a(\üst5 ), .b(\sağ_üst5 ), .c(\sağ_alt5 ), .d(alt5), .e(sol_alt5), .f(\sol_üst5 ), .g(orta5), .dp(1'b1));
  Seven_Seg seven_seg_3 (
    .a(\üst6 ), .b(\sağ_üst6 ), .c(\sağ_alt6 ), .d(alt6), .e(sol_alt6), .f(\sol_üst6 ), .g(orta6), .dp(1'b1));
  Seven_Seg seven_seg_4 (
    .a(\üst7 ), .b(\sağ_üst7 ), .c(\sağ_alt7 ), .d(alt7), .e(sol_alt7), .f(\sol_üst7 ), .g(orta7), .dp(1'b1));
  LED u_plus (.in(plus));
  LED led (.in(tunnel_t));
  LED led_2 (.in(tunnel));
  LED led_3 (.in(tunnel_t_t));
  Seven_Seg seven_seg_5 (
    .a(\üst ), .b(\sağ_üst ), .c(\sağ_alt ), .d(alt), .e(sol_alt), .f(\sol_üst ), .g(orta), .dp(1'b1));
  Button u__1 (.out(_1));
  Button u__4 (.out(_4));
  Button u__7 (.out(_7));
  Button plus_2 (.out(plus));
  Button button (.out(tunnel_t));
  Seven_Seg seven_seg_6 (
    .a(\üst1 ), .b(\sağ_üst1 ), .c(\sağ_alt1 ), .d(alt1), .e(sol_alt1), .f(\sol_üst1 ), .g(orta1), .dp(1'b1));
  Mul #(.Bits(4)) mul_1 (.a({Y3, Y2, Y1, Y0}), .b(in_6), .mul(mul_1_mul));
  Mul #(.Bits(4)) mul_2 (.a({B4, B3, B2, B1}), .b(in_4), .mul(mul_2_mul));
  Mul #(.Bits(4)) mul_3 (.a({A3, A2, A1, A0}), .b(in_2), .mul(mul_3_mul));
  Mul #(.Bits(4)) mul_4 (.a({I3, I2, I1, I0}), .b(in_1), .mul(mul_4_mul));
  Mul #(.Bits(4)) mul_5 (.a({M15, M14, M13, M12}), .b(in_14), .mul(mul_5_mul));
  Mul #(.Bits(4)) mul_6 (.a({M11, M10, M9, M8}), .b(in_12), .mul(mul_6_mul));
  Mul #(.Bits(4)) mul_7 (.a({M7, M6, M5, M4}), .b(in_10), .mul(mul_7_mul));
  Mul #(.Bits(4)) mul_8 (.a({M3, M2, M1, M0}), .b(in_9), .mul(mul_8_mul));
  Button u__2 (.out(_2));
  Button u__5 (.out(_5));
  Button u__8 (.out(_8));
  Button u__0 (.out(_0));
  Button u_C (.out(C));
  Button u_eq (.out(eq));
  Seven_Seg seven_seg_7 (
    .a(\üst2 ), .b(\sağ_üst2 ), .c(\sağ_alt2 ), .d(alt2), .e(sol_alt2), .f(\sol_üst2 ), .g(orta2), .dp(1'b1));
  Mul #(.Bits(8)) mul_9 (.a(mul_2_mul), .b(in_5), .mul(mul_9_mul));
  Mul #(.Bits(8)) mul_10 (.a(mul_5_mul), .b(in_15), .mul(mul_10_mul));
  Mul #(.Bits(8)) mul_11 (.a(mul_6_mul), .b(in_13), .mul(mul_11_mul));
  Mul #(.Bits(8)) mul_12 (.a(mul_7_mul), .b(in_11), .mul(mul_12_mul));
  Mul #(.Bits(8)) mul_13 (.a(mul_8_mul), .b(in_16), .mul(mul_13_mul));
  Mul #(.Bits(8)) mul_14 (.a(mul_1_mul), .b(in_7), .mul(mul_14_mul));
  Mul #(.Bits(8)) mul_15 (.a(mul_3_mul), .b(in_3), .mul(mul_15_mul));
  Mul #(.Bits(8)) mul_16 (.a(mul_4_mul), .b(in_8), .mul(mul_16_mul));
  Button u__3 (.out(_3));
  Button u__6 (.out(_6));
  Button u__9 (.out(_9));
  Button button_2 (.out(tunnel));
  Button button_3 (.out(tunnel_t_t));
  Seven_Seg seven_seg_8 (
    .a(\üst3 ), .b(\sağ_üst3 ), .c(\sağ_alt3 ), .d(alt3), .e(sol_alt3), .f(\sol_üst3 ), .g(orta3), .dp(1'b1));
  Add #(.Bits(16)) add_1 (.a(mul_10_mul), .b(mul_10_mul), .c_i(1'b0), .s(add_1_s));  // open: c_o
  LED u_error (.in(error));
  LED negatif (.in(eksi));
  Add #(.Bits(16)) add_2 (.a(mul_14_mul), .b(mul_14_mul), .c_i(1'b0), .s(add_2_s));  // open: c_o
  Add #(.Bits(16)) add_3 (.a(add_2_s), .b(mul_14_mul), .c_i(1'b0), .s(add_3_s));  // open: c_o
  Add #(.Bits(16)) add_4 (.a(add_1_s), .b(mul_10_mul), .c_i(1'b0), .s(add_4_s));  // open: c_o
  Add #(.Bits(16)) add_5 (.a(add_3_s), .b(mul_14_mul), .c_i(1'b0), .s(add_5_s));  // open: c_o
  Add #(.Bits(16)) add_6 (.a(mul_15_mul), .b(mul_16_mul), .c_i(1'b0), .s(add_6_s));  // open: c_o
  Add #(.Bits(16)) add_7 (.a(add_4_s), .b(mul_10_mul), .c_i(1'b0), .s(add_7_s));  // open: c_o
  Add #(.Bits(16)) add_8 (.a(mul_12_mul), .b(mul_13_mul), .c_i(1'b0), .s(add_8_s));  // open: c_o
  D_FF d_ff_1 (.D(plus), .C(clk1), .Q(d_ff_1_q));  // open: nQ
  D_FF d_ff_2 (.D(tunnel_t), .C(clk1), .Q(d_ff_2_q));  // open: nQ
  D_FF d_ff_3 (.D(tunnel), .C(clk1), .Q(d_ff_3_q));  // open: nQ
  D_FF d_ff_4 (.D(tunnel_t_t), .C(clk1), .Q(d_ff_4_q));  // open: nQ
  Add #(.Bits(16)) add_9 (.a(add_7_s), .b(mul_10_mul), .c_i(1'b0), .s(add_9_s));  // open: c_o
  Add #(.Bits(16)) add_10 (.a(add_5_s), .b(mul_14_mul), .c_i(1'b0), .s(add_10_s));  // open: c_o
  Add #(.Bits(16)) add_11 (.a(add_10_s), .b(mul_14_mul), .c_i(1'b0), .s(add_11_s));  // open: c_o
  Add #(.Bits(16)) add_12 (.a(add_6_s), .b(mul_9_mul), .c_i(1'b0), .s(add_12_s));  // open: c_o
  Add #(.Bits(16)) add_13 (.a(add_9_s), .b(mul_10_mul), .c_i(1'b0), .s(add_13_s));  // open: c_o
  Add #(.Bits(16)) add_14 (.a(add_8_s), .b(mul_11_mul), .c_i(1'b0), .s(add_14_s));  // open: c_o
  operation operation_1 (
    .x1(get1), .x2(get2), .plus(d_ff_1_q), .in_4(d_ff_2_q), .in_5(d_ff_3_q), .in_6(d_ff_4_q), .error(error),
    .eksi(eksi), .\çıktı (\operation_1_çıktı ));
  Add #(.Bits(16)) add_15 (.a(add_11_s), .b(mul_14_mul), .c_i(1'b0), .s(add_15_s));  // open: c_o
  Add #(.Bits(16)) add_16 (.a(add_13_s), .b(mul_10_mul), .c_i(1'b0), .s(add_16_s));  // open: c_o
  Add #(.Bits(16)) add_17 (.a(add_15_s), .b(mul_14_mul), .c_i(1'b0), .s(add_17_s));  // open: c_o
  Add #(.Bits(16)) add_18 (.a(add_16_s), .b(mul_10_mul), .c_i(1'b0), .s(add_18_s));  // open: c_o
  Add #(.Bits(16)) add_19 (.a(add_24_s), .b(add_14_s), .c_i(1'b0), .s(get1));  // open: c_o
  Div #(.Bits(16)) \binler_basamağı  (.a(\operation_1_çıktı ), .b(in_17), .q(out_23));  // open: r
  Add #(.Bits(16)) add_20 (.a(add_23_s), .b(add_12_s), .c_i(1'b0), .s(get2));  // open: c_o
  Add #(.Bits(16)) add_21 (.a(add_17_s), .b(mul_14_mul), .c_i(1'b0), .s(add_21_s));  // open: c_o
  Add #(.Bits(16)) add_22 (.a(add_18_s), .b(mul_10_mul), .c_i(1'b0), .s(add_22_s));  // open: c_o
  Div #(.Bits(16)) \yüzler_basamağı  (.a(\operation_1_çıktı ), .b(in_18), .q(\yüzler_basamağı_q ));  // open: r
  Div #(.Bits(16)) div_1 (.a(\yüzler_basamağı_q ), .b(in_20), .q(out_21), .r(out_24));
  Add #(.Bits(16)) add_23 (.a(add_21_s), .b(mul_14_mul), .c_i(1'b0), .s(add_23_s));  // open: c_o
  Add #(.Bits(16)) add_24 (.a(add_22_s), .b(mul_10_mul), .c_i(1'b0), .s(add_24_s));  // open: c_o
  Div #(.Bits(16)) \onlar_basamağı  (.a(\operation_1_çıktı ), .b(in_19), .q(\onlar_basamağı_q ), .r(out_25));
  Div #(.Bits(16)) div_2 (.a(\onlar_basamağı_q ), .b(in_19), .q(out_22), .r(out_26));
  decimal_to_bcd decimal_to_bcd_2 (
    ._1(_1), ._3(_3), ._2(_2), ._5(_5), ._4(_4), ._6(_6), ._7(_7), ._9(_9), ._8(_8), ._0(_0), .B0(b0),
    .B1(b1_t), .B2(b2_t), .B3(b3_t));

  // Other names for the same wires on the sheet: binler[15:0] = out_23; birler[15:0] = out_25; onlar[15:0] = out_26;
  //   yüzler[15:0] = out_24

  // Notes on the sheet:
  //   in_1: default 1
  //   in_2: default 10
  //   in_3: default 1
  //   in_4: default 10
  //   in_5: default 10
  //   in_6: default 10
  //   in_7: default 10
  //   in_8: default 1
  //   in_9: default 1
  //   in_10: default 10
  //   in_11: default 1
  //   in_12: default 10
  //   in_13: default 10
  //   in_14: default 10
  //   in_15: default 10
  //   in_16: default 1
  //   in_17: default 1000
  //   in_18: default 100
  //   in_19: default 10
  //   in_20: default 10
endmodule
