// Digital circuit adder.dig as structural Verilog
module adder (
  input  [3:0] b0,
  input  [3:0] b1,
  input  [3:0] b2,
  input  [3:0] b3,
  output [3:0] \çıktı 
);

  wire add_1_c_o;
  wire [3:0] add_1_s, add_2_s;

  Add #(.Bits(4)) add_1 (.a(b0), .b(b1), .c_i(1'b0), .s(add_1_s), .c_o(add_1_c_o));
  Add #(.Bits(4)) add_2 (.a(add_1_s), .b(b2), .c_i(1'b0), .s(add_2_s));  // open: c_o
  Add #(.Bits(4)) add_3 (.a(add_2_s), .b(b3), .c_i(1'b0), .s(\çıktı ));  // open: c_o

  // Notes on the sheet:
  //   b0: default 1
  //   b1: default 2
  //   b2: default 4
  //   b3: default 8
endmodule
