// Digital circuit decimal_to_bcd.dig as structural Verilog
module decimal_to_bcd (
  input  _1,
  input  _3,
  input  _2,
  input  _4,
  input  _5,
  input  _6,
  input  _7,
  input  _8,
  input  _9,
  input  _0,
  output B0,
  output B1,
  output B2,
  output B3
);

  or or_1 (B0, _1, _3, _5, _7, _9);
  or or_2 (B1, _2, _3, _6, _7);
  or or_3 (B2, _4, _5, _6, _7);
  or or_4 (B3, _8, _9);
endmodule
