// Digital circuit emb.dig as structural Verilog
module emb (
  input  b3,
  input  b2,
  input  b1,
  input  b0,
  output \sağ_alt ,
  output orta,
  output \sağ_üst ,
  output \sol_üst ,
  output \üst ,
  output sol_alt,
  output alt
);

  wire and_1_out, and_2_out, and_3_out, and_4_out, and_5_out, and_6_out, and_7_out, and_8_out, and_9_out,
       and_10_out, and_11_out, and_12_out, and_13_out, and_14_out, and_15_out, and_16_out, and_17_out,
       and_18_out, and_19_out, and_20_out, and_21_out, and_22_out, and_23_out, and_24_out, and_25_out,
       and_26_out, and_27_out, and_28_out, and_29_out, and_30_out, and_31_out, and_32_out, and_33_out,
       and_34_out, and_35_out, and_36_out, and_37_out, and_38_out, and_39_out, and_40_out, and_41_out,
       not_1_out, not_2_out, not_3_out, not_4_out, not_5_out;

  not not_1 (not_1_out, 1'b1);
  not not_2 (not_2_out, b3);
  not not_3 (not_3_out, b2);
  not not_4 (not_4_out, b1);
  not not_5 (not_5_out, b0);
  and and_1 (and_1_out, not_1_out, not_5_out, b3);
  and and_2 (and_2_out, not_1_out, b1, b2);
  and and_3 (and_3_out, not_5_out, not_4_out, not_3_out);
  and and_4 (and_4_out, b0, b2, not_2_out);
  and and_5 (and_5_out, not_4_out, not_3_out, b3);
  and and_6 (and_6_out, b1, not_2_out);
  and and_7 (and_7_out, not_1_out, b0, not_4_out, b3);
  and and_8 (and_8_out, not_1_out, not_5_out, not_3_out);
  and and_9 (and_9_out, not_5_out, not_4_out, not_2_out);
  and and_10 (and_10_out, b0, b1, not_2_out);
  and and_11 (and_11_out, not_4_out, not_3_out);
  and and_12 (and_12_out, not_3_out, not_2_out);
  and and_13 (and_13_out, not_1_out, b0, not_4_out);
  and and_14 (and_14_out, not_1_out, not_3_out, b3);
  and and_15 (and_15_out, b0, not_2_out);
  and and_16 (and_16_out, not_4_out, not_3_out);
  and and_17 (and_17_out, b2, not_2_out);
  and and_18 (and_18_out, not_1_out, b0, b1, not_3_out);
  and and_19 (and_19_out, not_1_out, not_5_out, b2, b3);
  and and_20 (and_20_out, not_1_out, not_4_out, b3);
  and and_21 (and_21_out, b0, not_4_out, b2, not_2_out);
  and and_22 (and_22_out, not_5_out, not_4_out, not_3_out);
  and and_23 (and_23_out, not_5_out, b1, not_2_out);
  and and_24 (and_24_out, b1, not_3_out, not_2_out);
  and and_25 (and_25_out, not_4_out, not_3_out, b3);
  and and_26 (and_26_out, not_1_out, b1, b3);
  and and_27 (and_27_out, not_1_out, b2, b3);
  and and_28 (and_28_out, not_5_out, not_4_out, not_3_out);
  and and_29 (and_29_out, not_5_out, b1, not_2_out);
  and and_30 (and_30_out, not_1_out, not_5_out, not_4_out);
  and and_31 (and_31_out, not_1_out, b1, b3);
  and and_32 (and_32_out, not_5_out, not_4_out, not_3_out);
  and and_33 (and_33_out, not_5_out, b2, not_2_out);
  and and_34 (and_34_out, not_4_out, b2, not_2_out);
  and and_35 (and_35_out, not_4_out, not_3_out, b3);
  and and_36 (and_36_out, not_1_out, b0, b3);
  and and_37 (and_37_out, not_1_out, b1, b3);
  and and_38 (and_38_out, not_5_out, b1, not_2_out);
  and and_39 (and_39_out, b1, not_3_out, not_2_out);
  and and_40 (and_40_out, not_4_out, b2, not_2_out);
  and and_41 (and_41_out, not_4_out, not_3_out, b3);
  or or_1 (\üst , and_1_out, and_2_out, and_3_out, and_4_out, and_5_out, and_6_out);
  or or_2 (\sağ_üst , and_7_out, and_8_out, and_9_out, and_10_out, and_11_out, and_12_out);
  or or_3 (\sağ_alt , and_13_out, and_14_out, and_15_out, and_16_out, and_17_out);
  or or_4 (alt, and_18_out, and_19_out, and_20_out, and_21_out, and_22_out, and_23_out, and_24_out, and_25_out);
  or or_5 (sol_alt, and_26_out, and_27_out, and_28_out, and_29_out);
  or or_6 (\sol_üst , and_30_out, and_31_out, and_32_out, and_33_out, and_34_out, and_35_out);
  or or_7 (orta, and_36_out, and_37_out, and_38_out, and_39_out, and_40_out, and_41_out);

  // Notes on the sheet:
  //   1
  //   2
  //   3
  //   4
  //   5
  //   6
  //   7
endmodule
