// Digital circuit opclk.dig as structural Verilog
module opclk (
  input  plus,
  input  in_2,
  input  in_3,
  input  in_4,
  input  C,
  output clk1
);

  or or_1 (clk1, plus, in_2, C, in_3, in_4);
endmodule
