// Digital circuit operation.dig as structural Verilog
module operation (
  input  [15:0] x1,
  input  [15:0] x2,
  input  plus,
  input  in_4,
  input  in_5,
  input  in_6,
  output error,
  output eksi,
  output [15:0] \çıktı 
);

  wire any, eksi_t, hata, nulldiv, overflow;
  wire [1:0] priorityencoder_1_num;
  wire [15:0] \bölme , kalan, toplam, \çarpma , \çıkarma ;
  wire [31:16] mul_1_mul;

  Add #(.Bits(16)) add_1 (.a(x1), .b(x2), .c_i(1'b0), .s(toplam), .c_o(hata));
  Sub #(.Bits(16)) sub_1 (.a(x1), .b(x2), .c_i(1'b0), .s(\çıkarma ), .c_o(eksi_t));
  Div #(.Bits(16)) div_1 (.a(x1), .b(x2), .q(\bölme ), .r(kalan));
  nor nor_1 (nulldiv, x2[0], x2[1], x2[2], x2[3], x2[4], x2[5], x2[6], x2[7], x2[9], x2[10], x2[11], x2[12], x2[13], x2[14], x2[15], x2[8]);
  PriorityEncoder #(.Selector_Bits(2)) priorityencoder_1 (
    .in0(plus), .in1(in_4), .in2(in_5), .in3(in_6), .num(priorityencoder_1_num), .any(any));
  Multiplexer #(.Selector_Bits(2), .Bits(16)) multiplexer_1 (
    .sel(priorityencoder_1_num), .in_0(toplam), .in_1(\çıkarma ), .in_2(\çarpma ), .in_3(\bölme ),
    .out(\çıktı ));
  Mul #(.Bits(16)) mul_1 (.a(x1), .b(x2), .mul({mul_1_mul, \çarpma }));
  and and_1 (eksi, in_4, eksi_t);
  or or_1 (overflow, mul_1_mul[16], mul_1_mul[17], mul_1_mul[18], mul_1_mul[19], mul_1_mul[20], mul_1_mul[21], mul_1_mul[22], mul_1_mul[23], mul_1_mul[25], mul_1_mul[26], mul_1_mul[27], mul_1_mul[28], mul_1_mul[29], mul_1_mul[30], mul_1_mul[31], mul_1_mul[24]);
  or or_2 (error, hata, nulldiv, overflow);

  // Other names for the same wires on the sheet: tunnel = in_5; tunnel_t = in_4; tunnel_t_t = in_6

  // Notes on the sheet:
  //   x1: default 8
  //   x2: default 3
endmodule
